# Fritzing sketch greenbox (saved by Fritzing 0.9.9b)
breadboards: 1

parts:
  Part1 = Arduino MKR WiFi 1010
  U1 = TEMPERATURE-SENSOR [package=to-92]
  HC-SR04_Sensor_1 = HC-SR04 Ultrasonic Distance Sensor
  Part2 = TFT 1.8 inch 160x128 w microSD [part_number=358]
  U2 = WS2812 RGB LED strip
  R1 = Resistor [tolerance=±5% power=0.25 resistance=220 package=THT]

nets:
  N1: Part1.D0, HC-SR04_Sensor_1.TRIG
  N2: Part1.D1, U1.ADJ
  N3: Part1.D4_PWM, R1.Pin_1
  N4: Part1.D5_PWM, HC-SR04_Sensor_1.ECHO
  N5: Part1.D6, Part2.CARDCS
  N6: Part1.D7, Part2.TFTDC
  N7: Part1.D8_MOSI, Part2.TFTCS
  N8: Part1.D9_SCK, Part2.SCLK
  N9: Part1.RESET, Part2.RESET
  GND: Part1.GND, U1.GND, HC-SR04_Sensor_1.GND, Part2.GND, U2.GND
  N10: Part1.VCC, Part2.LITE
  VCC: Part1.5V, U1.VCC, HC-SR04_Sensor_1.VCC, Part2.+5V, U2.VCC
  N11: U2.DOUT, R1.Pin_0

notes:
  Note
  dht22 -> generic temp sensor(actual one is dht22 4pin sensor)
  1.8" tft -> generic 1.8 display(image is in different pin order than actual one)
  fix
  - ledstrip resistor value
  - display pin order is different from actuala one(can't find exact same display in fritzing)
  Hardware List
  - Arduino MKR 1010 Board for wireless communication
  - DHT22 Sensor for temperature & humidity
  - HC-SR04Ultrasonic Sensor for proximity
  - Generic LED Strip
  - Generic 1.8" TFT Display

custom parts:
  Arduino MKR WiFi 1010: This is the newest version of the MKR 1000 WIFI, but with an ESP32 module on board made by U-BLOX.
  TFT 1.8 inch 160x128 w microSD: This lovely little display breakout is the best way to add a small, colorful and bright display to any project. Since the display uses 4-wire SPI to communicate and has its own pixel-addressable frame buffer, it can be used with every kind of microcontroller. Even a very small one with low memory and few pins available! The 1.8" display has 128x160 color pixels.
  WS2812 RGB LED strip: WS2812 strip
